# Fritzing sketch CAN_RemoteStart (saved by Fritzing 0.9.3b)
breadboards: 1

parts:
  R1 = Resistor [tolerance=±5% resistance=10k package=THT]
  PCB1 = Arduino Shield PCB  # not connected
  Arduino1 = Arduino Uno (Rev3)
  S2 = Pushbutton [package="[SMD]"]
  S3 = Pushbutton [package="[SMD]"]
  R2 = Resistor [tolerance=±5% resistance=10k package=THT]
  LED1 = smd LED [color="Green (570nm)" package="0603 [SMD]"]
  LED2 = smd LED [color="Red (633nm)" package="0603 [SMD]"]
  R3 = Resistor [tolerance=±5% resistance=330 package=THT]
  R4 = Resistor [tolerance=±5% resistance=330 package=THT]

nets:
  N1: R1.Pin_0, Arduino1.D4, S3.Pin_1, S3.Pin_2
  N2: R1.Pin_1, Arduino1.GND, R2.Pin_1, R3.Pin_1, R4.Pin_1
  N3: Arduino1.D2, LED2.cathode
  N4: Arduino1.D3_PWM, LED1.cathode
  N5: Arduino1.D5_PWM, S2.Pin_1, S2.Pin_2, R2.Pin_0
  N6: Arduino1.5V, S2.Pin_3, S2.Pin_4, S3.Pin_3, S3.Pin_4
  N7: LED1.anode, R4.Pin_0
  N8: LED2.anode, R3.Pin_0

notes:
  In this example, a pushbutton is used as a digital input and an LED is a digital output.
  Related example: http://arduino.cc/en/Tutorial/Button

custom parts:
  Arduino Shield PCB: Plain PCB Shaped to fit an Arduino "Shield"

// code stored in the sketch: Button.ino
/*
  Button
 
 Turns on and off a light emitting diode(LED) connected to digital  
 pin 13, when pressing a pushbutton attached to pin 2. 
 
 
 The circuit:
 * LED attached from pin 13 to ground 
 * pushbutton attached to pin 2 from +5V
 * 10K resistor attached to pin 2 from ground
 
 * Note: on most Arduinos there is already an LED on the board
 attached to pin 13.
 
 
 created 2005
 by DojoDave <http://www.0j0.org>
 modified 30 Aug 2011
 by Tom Igoe
 
 This example code is in the public domain.
 
 http://www.arduino.cc/en/Tutorial/Button
 */

// constants won't change. They're used here to 
// set pin numbers:
const int buttonPin = 2;     // the number of the pushbutton pin
const int ledPin =  13;      // the number of the LED pin

// variables will change:
int buttonState = 0;         // variable for reading the pushbutton status

void setup() {
  // initialize the LED pin as an output:
  pinMode(ledPin, OUTPUT);      
  // initialize the pushbutton pin as an input:
  pinMode(buttonPin, INPUT);     
}

void loop(){
  // read the state of the pushbutton value:
  buttonState = digitalRead(buttonPin);

  // check if the pushbutton is pressed.
  // if it is, the buttonState is HIGH:
  if (buttonState == HIGH) {     
    // turn LED on:    
    digitalWrite(ledPin, HIGH);  
  } 
  else {
    // turn LED off:
    digitalWrite(ledPin, LOW); 
  }
}
